# Fritzing sketch fritzing_design_v1 (saved by Fritzing 0.9.3b)
breadboards: 1

parts:
  Part1 = Arduino Nano (Rev3.0)
  M1 = DC Motor
  M2 = DC Motor
  L298N1 = L298N DC motor driver
  GY1 = MPU-6050 Board GY-521 [form="♀ (female)" package=THT]

nets:
  N1: Part1.D3, L298N1.ENA
  N2: Part1.D4, L298N1.IN1
  N3: Part1.D5, L298N1.IN2
  N4: Part1.D6, L298N1.ENB
  N5: Part1.D7, L298N1.IN3
  N6: Part1.D8, L298N1.IN4
  N7: Part1.A5, GY1.pin3
  N8: Part1.A4, GY1.pin4
  N9: M1.pin_1, L298N1.OUT3
  N10: M1.pin_2, L298N1.OUT4
  N11: M2.pin_1, L298N1.OUT1
  N12: M2.pin_2, L298N1.OUT2

custom parts:
  L298N DC motor driver: 2x DC motor driver with 78M05 positive voltage regulator (7..35 V) L298N: max 46 V, 2 A Set 5 V Enable jumper to enable 5 V regultor (needed for the L298N) and +5 V output at screw terminal or supply external +5 V at screw terminal Set ENA and/or ENB to +5 V to enable motor permanently or supply ENA and/or ENB with PWM signal IN1 and IN2 set rotation directory for motor A (OUT1/OUT2) IN2 and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
  MPU-6050 Board GY-521: Acelerometro y Giroscopio MPU-6050 Board GY-521
